# Fritzing sketch HeaterBrdBoard2 (saved by Fritzing 0.9.3b)
circuit board: 8.46667cm x 5.64444cm
breadboards: 1
perfboards: 1

parts:
  Part1 = Arduino Nano (Rev3.0)
  S1 = Pushbutton [package="[THT]"]
  RHT1 = Humidity and Temperature Sensor RHT03  # not connected
  S2 = Pushbutton [package="[THT]"]
  S3 = Pushbutton [package="[THT]"]
  DS1 = DS18B20 1-Wire Temperature Sensor [part_number=DS18B20]  # not connected
  DS2 = DS18B20 1-Wire Temperature Sensor [part_number=DS18B20]  # not connected
  R4 = Resistor [tolerance=±5% resistance=10k package=THT]
  R5 = Resistor [tolerance=±20% resistance=4.7k package=THT]
  Part2 = OLED Monochrome 128x64 1.3 inch [part_number=938]  # not connected
  C1 = Electrolytic Capacitor [capacitance=200µF voltage=35V package="100 mil [THT, electrolytic]"]
  J1 = female pin header, 7 pins [form="♀ (female)"]
  J2 = female pin header, 4 pins [form="♀ (female)"]
  J3 = female pin header, 3 pins [form="♀ (female)"]
  J4 = female pin header, 3 pins [form="♀ (female)"]
  J5 = female pin header, 3 pins [form="♀ (female)"]
  J6 = female pin header, 3 pins [form="♀ (female)"]
  J7 = female pin header, 3 pins [form="♀ (female)"]
  S4 = Pushbutton [package="[THT]"]
  Part3 = Arduino Nano (Rev3.0)  # not connected
  J8 = female pin header, 6 pins [form="♀ (female)"]  # not connected
  J9 = female pin header, 3 pins [form="♀ (female)"]  # not connected
  J10 = female pin header, 3 pins [form="♀ (female)"]  # not connected
  J11 = female pin header, 3 pins [form="♀ (female)"]  # not connected
  C2 = Electrolytic Capacitor [capacitance=200µF voltage=35V package="100 mil [THT, electrolytic]"]
  R6 = Resistor [tolerance=±20% resistance=4.7k package=THT]
  R7 = Resistor [tolerance=±20% resistance=4.7k package=THT]
  C3 = Electrolytic Capacitor [capacitance=200µF voltage=35V package="100 mil [THT, electrolytic]"]
  J12 = female pin header, 14 pins [form="♀ (female)"]  # not connected

nets:
  N1: Part1.GND, S1.Pin_3, S1.Pin_4, S3.Pin_3, S3.Pin_4, C1.-, J1.pin1, J2.pin1, J3.pin3, J4.pin3, J5.pin3, J6.pin3, J7.pin3, S4.Pin_3, S4.Pin_4
  N2: Part1.D2, S1.Pin_1, S1.Pin_2
  N3: Part1.D3, S2.Pin_1, S2.Pin_2
  N4: Part1.D4, S4.Pin_1, S4.Pin_2
  N5: Part1.D6, S3.Pin_1, S3.Pin_2
  N6: Part1.D8, J1.pin5
  N7: Part1.D9, J1.pin4
  N8: Part1.D10, J1.pin3
  N9: Part1.D11/MOSI, J1.pin6
  N10: Part1.D12/MISO, J1.pin7
  N11: Part1.VIN, R4.Pin_1, R5.Pin_1, C1.+, J1.pin2, J2.pin4, J3.pin1, J4.pin1, J5.pin2, J6.pin2, J7.pin2
  N12: Part1.A5, R5.Pin_0, J3.pin2, J4.pin2
  N13: Part1.A4, J5.pin1
  N14: Part1.A3, J6.pin1
  N15: Part1.A2, J7.pin1
  N16: Part1.A0, R4.Pin_0, J2.pin3
  N17: S2.Pin_3, S2.Pin_4
  N18: C2.-, C3.-
  N19: C2.+, C3.+
  N20: R6.Pin_0, R7.Pin_0

custom parts:
  OLED Monochrome 128x64 1.3 inch: These displays are small, only about 1.3" diagonal, but very readable due to the high contrast of an OLED display. This display is made of 128x64 individual white OLED pixels, each one is turned on or off by the controller chip. Because the display makes its own light, no backlight is required. This reduces the power required to run the OLED and is why the display has such high contrast; we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
