# Fritzing sketch protoBoard (saved by Fritzing 0.9.3b)
circuit board: 7cm x 5cm
breadboards: 1
perfboards: 1

parts:
  C4 = Electrolytic Capacitor [capacitance=200µF voltage=35V package="100 mil [THT, electrolytic]"]
  J13 = female pin header, 3 pins [form="♀ (female)"]
  J14 = female pin header, 3 pins [form="♀ (female)"]
  J15 = female pin header, 6 pins [form="♀ (female)"]
  J16 = female pin header, 3 pins [form="♀ (female)"]
  Part4 = Arduino Nano (Rev3.0)
  R8 = Resistor [tolerance=±20% resistance=4.7k package=THT]
  R9 = Resistor [tolerance=±20% resistance=4.7k package=THT]
  J17 = female pin header, 14 pins [form="♀ (female)"]
  C5 = Electrolytic Capacitor [capacitance=200µF voltage=35V package="100 mil [THT, electrolytic]"]
  J18 = female pin header, 5 pins [form="♀ (female)"]
  C6 = Electrolytic Capacitor [capacitance=200µF voltage=35V package="100 mil [THT, electrolytic]"]

nets:
  N1: C4.-, J13.pin3, J14.pin3, J15.pin6, J16.pin3, Part4.GND, J17.pin1, J17.pin8, C5.-, J18.pin1
  N2: C4.+, J13.pin1, J14.pin1, J15.pin1, J16.pin1, Part4.5V, R8.Pin_1, R9.Pin_1, J17.pin9, C5.+, J18.pin5, C6.+
  N3: J13.pin2, J14.pin2, Part4.A5, R9.Pin_0
  N4: J15.pin3, Part4.A4
  N5: J15.pin4, Part4.A3
  N6: J15.pin5, Part4.A2
  N7: J16.pin2, Part4.A0, R8.Pin_0
  N8: Part4.D3, J17.pin2
  N9: Part4.D4, J17.pin3
  N10: Part4.D5, J17.pin4
  N11: Part4.D7, J17.pin7
  N12: Part4.D8, J17.pin12
  N13: Part4.D9, J17.pin11
  N14: Part4.D10, J17.pin10
  N15: Part4.D11/MOSI, J17.pin13
  N16: Part4.D12/MISO, J17.pin14
